# Fritzing sketch brush (saved by Fritzing 0.8.7b)
circuit board: 6.86961cm x 5.48946cm
breadboards: 1

parts:
  Part1 = Arduino Uno (Rev3)
  Part2 = IMU Digital Combo Board 6DOF
  LED1 = LED - 5mm [color="Red (633nm)" package="5 mm [THT]"]
  R1 = Resistor [tolerance=±5% resistance=220 package=THT]

nets:
  GND: Part1.GND, Part2.GND, LED1.cathode, LED1.anode, R1.Pin_0
  3V3: Part1.3V3, Part2.3.3V, R1.Pin_1
